# Fritzing sketch server-ble (saved by Fritzing 0.9.5d)
breadboards: 2

parts:
  ESP32S = DOIT Esp32 DevKit v1 (30 pins long, 11 pins width) [part_number=ESP32S]
  Arduino_Nano = Arduino Nano (Rev3.0) (ICSP)
  LCD2004-I2C1 = LCD2004-I2C
  Logic_Level = TXB0108 8-channel Bi-directional Logic Level Converter
  Power_Supply_1 = DC Power [voltage=24V]
  24V_Relay = Keyes Relay [package=THT]
  Line_Tracing_Sensor = KY-033 Tracing Black White Line Hunting Sensor Module For Arduino
  Stepper_Motor_Closed_Loop = Stepper Motor Closed Loop [part_number=4001 package="DIP (Dual Inline) [THT]"]
  2HSS57 = DOIT Esp32 DevKit v1 (30 pins long, 11 pins width) [part_number=ESP32S-PIN30]
  5V_YwRobot_Power_Supply = YwRobot Breadboard Power Supply [part_number=545043]

nets:
  N1: ESP32S.3V3, Logic_Level.VCCA
  GND: ESP32S.GND, Arduino_Nano.GND, LCD2004-I2C1.GND, Logic_Level.GND, Power_Supply_1.V-, 24V_Relay.ground, Line_Tracing_Sensor.GND, 2HSS57.GND, 5V_YwRobot_Power_Supply.GND#13, 5V_YwRobot_Power_Supply.GND#14
  N2: ESP32S.D18, Logic_Level.A1
  N3: ESP32S.D19, Logic_Level.A2
  N4: ESP32S.D21, Logic_Level.A3
  N5: ESP32S.D22, Logic_Level.A4
  N6: ESP32S.D23, Logic_Level.OE
  VIN: ESP32S.VIN, Arduino_Nano.VIN, LCD2004-I2C1.VCC, Logic_Level.VCCB, 24V_Relay.power, Line_Tracing_Sensor.V+, 2HSS57.PUL+, 2HSS57.DIR+, 5V_YwRobot_Power_Supply.VCC#9, 5V_YwRobot_Power_Supply.VCC#10
  N7: Arduino_Nano.D2, 2HSS57.DIR-
  N8: Arduino_Nano.D3, 2HSS57.PUL-
  N9: Arduino_Nano.D4, 24V_Relay.signal
  N10: Arduino_Nano.D9, Line_Tracing_Sensor.S
  N11: Arduino_Nano.A5, Logic_Level.B4
  N12: Arduino_Nano.A4, Logic_Level.B3
  N13: LCD2004-I2C1.SDA, Logic_Level.B1
  N14: LCD2004-I2C1.SCL, Logic_Level.B2
  N15: Power_Supply_1.V+, 24V_Relay.NO
  N16: 24V_Relay.C, 2HSS57.+VDC
  N17: Stepper_Motor_Closed_Loop.A-, 2HSS57.A-
  N18: Stepper_Motor_Closed_Loop.A+, 2HSS57.A+
  N19: Stepper_Motor_Closed_Loop.B-, 2HSS57.B-
  N20: Stepper_Motor_Closed_Loop.B+, 2HSS57.B+
  +5V: Stepper_Motor_Closed_Loop.+5V, 2HSS57.VCC
  N21: Stepper_Motor_Closed_Loop.PA+, 2HSS57.EA+
  N22: Stepper_Motor_Closed_Loop.GND, 2HSS57.EGND
  N23: Stepper_Motor_Closed_Loop.PB-, 2HSS57.EB-
  N24: Stepper_Motor_Closed_Loop.PB+, 2HSS57.EB+
  N25: Stepper_Motor_Closed_Loop.PA-, 2HSS57.EA-
  N26: 5V_YwRobot_Power_Supply.VCC#5, 5V_YwRobot_Power_Supply.VCC#6
  N27: 5V_YwRobot_Power_Supply.GND#11, 5V_YwRobot_Power_Supply.GND#12

custom parts:
  DOIT Esp32 DevKit v1 (30 pins long, 11 pins width): The DOIT Esp32 DevKit v1 is one of the development board created by DOIT to evaluate the ESP-WROOM-32 module. It is based on the ESP32 microcontroller that boasts Wifi, Bluetooth, Ethernet and Low Power support all in a single chip. (vanepp) made breadboard work, adjusted pin numbering and labels and reduced size of schematic and cleaned up pcb. This chip is 30pins long (2 x15) and 11 pins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
  LCD2004-I2C: A standard character display with 4x20 characters. Comes in many colors with LCM2004 IIC attached.
  TXB0108 8-channel Bi-directional Logic Level Converter: Because the Arduino (and Basic Stamp) are 5V devices, and most modern sensors, displays, flash cards and modes are 3.3V-only, many makers find that they need to perform level shifting/conversion to protect the 3.3V device from 5V. Although one can use resistors to make a divider, for high speed transfers, the resistors can add a lot of slew and cause havoc that is tough to debug. For that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
  Keyes Relay: The Keyes 5V relay module is suitable for SCM development, home appliance control. It uses a 5V~12V TIL control signal which can control DC / AC signal.
  KY-033 Tracing Black White Line Hunting Sensor Module For Arduino: Tracing Black White Line Hunting Sensor Module For Arduino Description: This is KY-033 tracking sensor. The KY-033 measures the intensity of infrared radiation and delivers it as an analog output voltage. Features: Operating voltage: 2.5 - 12V(cannot over12V) working current: 18mA-20mA at 5V Enhanced accuracy Documents: http://www.vishay.com/docs/83760/tcrt5000.pdf
  Stepper Motor Closed Loop: 4001 4 x 2 Input NOR Gate as a single part
  DOIT Esp32 DevKit v1 (30 pins long, 11 pins width): The DOIT Esp32 DevKit v1 is one of the development board created by DOIT to evaluate the ESP-WROOM-32 module. It is based on the ESP32 microcontroller that boasts Wifi, Bluetooth, Ethernet and Low Power support all in a single chip. (vanepp) made breadboard work, adjusted pin numbering and labels and reduced size of schematic and cleaned up pcb. This chip is 30pins long (2 x15) and 11 pins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
  YwRobot Breadboard Power Supply: The YwRobot Breadboard Power Supply (MB-V2) has two power rails; they can be 5V or 3V3. Power to the module can be provided through the female USB socket or through the A10 (female) 2.1mm power jack.
