# Fritzing sketch server (saved by Fritzing 0.9.4)
breadboards: 1

parts:
  Part2 = Arduino Ethernet Shield (Rev3)
  R1 = Rotary Potentiometer (Small) [maximum_resistance=100kΩ package=THT]
  U1 = LCD-16X2 [package=lcd-16x2_noholes]
  R2 = Resistor [tolerance=±5% resistance=220 package="0805 [SMD]"]

nets:
  5V: Part2.5V, R1.leg1, U1.VDD, R2.Pin_0
  N1: Part2.D8, U1.E
  N2: Part2.PWM_D9, U1.RS
  GND: Part2.GND, R1.leg2, U1.VSS, U1.R_W, U1.K
  N3: Part2.D2, U1.DB7
  N4: Part2.PWM_D5, U1.DB6
  N5: Part2.PWM_D6, U1.DB5
  N6: Part2.D7, U1.DB4
  N7: R1.wiper, U1.VO
  N8: U1.A, R2.Pin_1
